# Fritzing sketch ServerControll (saved by Fritzing 0.9.3b)
breadboards: 1

parts:
  Bauteil1 = Arduino Uno (Rev3) - ICSP
  R2 = Resistor [tolerance=±5% resistance=470 package=THT]
  Q2 = NPN-Transistor [package="TO92 [THT]"]
  U4 = G3VM-61E1 [package=g3vm-61e1]
  R4 = Resistor [tolerance=±5% resistance=1k package="1206 [SMD]"]

nets:
  N1: Bauteil1.GND, R2.Pin_1, Q2.E, U4.P$5
  N2: Bauteil1.D2, Q2.C
  N3: Bauteil1.D3_PWM, R4.Pin_0
  N4: Bauteil1.5V, U4.P$4
  N5: U4.P$6, R4.Pin_1

notes:
  Server Power Led + -
  Server Power Switch Pin
